# Fritzing sketch OVMS-OBD2-T26A-Cable (saved by Fritzing 1.0.5)
circuit board: 4.99395cm x 4.84948cm

parts:
  T26 = double row male pin header, 26 pins [form="♂ (male)"]
  OBD2 = OBDII [package=obdii]
  DB9-F = DB9 Connector [package=db9]

nets (from the schematic view):
  N1: T26.pin1, DB9-F.9
  N2: T26.pin2, DB9-F.6
  N3: T26.pin14, DB9-F.8
  N4: T26.pin26, OBD2.CHASGND, DB9-F.3
  N5: OBD2.CANHIGH, DB9-F.7
  N6: OBD2.CANLOW, DB9-F.2
